# Fritzing sketch EsquemaHorta (saved by Fritzing 0.9.4)
breadboards: 1

parts:
  U1 = NodeMCU V3.0 [part_number=3]
  DS1 = DS18B20 1-Wire Temperature Sensor [part_number=DS18B20]
  DS2 = DS18B20 1-Wire Temperature Sensor [part_number=DS18B20]
  YF-S201_Flow_Meter1 = YF-S201 Water Flow Meter [part_number=1]
  R1 = Photocell (LDR) [package=THT]
  DHT1 = DHT22 Humidity and Temperature Sensor [part_number=4]
  R2 = Resistor [tolerance=±5% resistance=5k package="0402 [SMD]"]
  R3 = Resistor [tolerance=±5% resistance=5k package="2010 [SMD]"]
  R4 = Resistor [tolerance=±5% resistance=10k package="2010 [SMD]"]
  Grove_Ultrasonic_Ranger1 = Grove Ultrasonic Ranger [part_number=5]
  Grove3 = Grove OLED 128x96 [part_number=7]
  YF-S201_Flow_Meter2 = YF-S201 Water Flow Meter [part_number=2]
  microSD1 = MicroSD Card Module [part_number=6]
  ZS-042_RTC1 = ZS-042 RTC Module

nets:
  N1: U1.D1, Grove3.SCL, ZS-042_RTC1.SCL
  N2: U1.D2, Grove3.SDA, ZS-042_RTC1.SDA
  N3: U1.D3, Grove_Ultrasonic_Ranger1.SIG
  N4: U1.D4, DS1.DQ, DS2.DQ, R2.Pin_0
  VCC: U1.3V3, DS1.VDD, DS2.VDD, R1.pin_0, DHT1.VDD, R2.Pin_1, Grove_Ultrasonic_Ranger1.VCC, Grove3.VCC, microSD1.VCC, ZS-042_RTC1.VCC
  GND: U1.GND#6, U1.GND#13, U1.GND#16, U1.GND#33, DS1.GND, DS2.GND, YF-S201_Flow_Meter1.GND, DHT1.GND, R3.Pin_1, Grove_Ultrasonic_Ranger1.GND, Grove3.GND, YF-S201_Flow_Meter2.GND, microSD1.GND, ZS-042_RTC1.GND
  N5: U1.D5, microSD1.SCK
  N6: U1.D6, microSD1.MISO
  N7: U1.D7, microSD1.MOSI
  N8: U1.D8, microSD1.CS
  VCC_2: U1.Vin, YF-S201_Flow_Meter1.VCC, YF-S201_Flow_Meter2.VCC
  N9: U1.SC, YF-S201_Flow_Meter1.SIG
  N10: U1.S1, YF-S201_Flow_Meter2.SIG
  N11: U1.S3, DHT1.DATA, R4.Pin_1
  N12: U1.A0, R1.pin_1, R3.Pin_0

notes:
  Verificar conexão de sensor liquido

custom parts:
  NodeMCU V3.0: ESP8266 based NodeMCU
  YF-S201 Water Flow Meter: The YF-S201 Flow Meter. The input voltage is 5V to 24V (DC).
  Grove Ultrasonic Ranger: Ultrasonic Ranger, Grove connector.
